# Fritzing sketch Protoboard (saved by Fritzing 0.9.5d)
breadboards: 2

parts:
  M1 = DOIT Esp32 DevKit v1 (30 pins long, 11 pins width) [part_number=ESP32S-PIN30]
  Componente2 = Adafruit VL530X Time of Flight Distance Sensor [part_number="Adafruit #3317"]
  Componente3 = QMC5883L - Triple Axis Magnetometer Breakout
  M2 = DC Motor
  M3 = DC Motor
  M4 = DC Motor
  M5 = DC Motor
  S1 = H-Bridge with L298N
  U1 = SWITCH_SPDT [package=kps-1290]
  BAT1 = LIPO-2000mAh [package=lipo-2000]
  U2 = LM2596 step down module

nets:
  VCC: M1.3V3, Componente2.VCC, Componente3.VCC
  GND: M1.GND, Componente2.GND, Componente3.GND, S1.GND, BAT1.-, U2.IN-, U2.OUT-
  N1: M1.D21, Componente2.SDA, Componente3.SDA
  N2: M1.D22, Componente2.SCL, Componente3.SCL
  N3: M1.D25, S1.ENB
  N4: M1.D26, S1.IN4
  N5: M1.D27, S1.IN3
  N6: M1.D14, S1.IN2
  N7: M1.D12, S1.IN1
  N8: M1.D13, S1.ENA
  N9: M1.VIN, U2.OUT+
  N10: M2.pin_1, M3.pin_1, S1.M2-02
  N11: M2.pin_2, M3.pin_2, S1.M2-01
  N12: M4.pin_1, M5.pin_1, S1.M1-02
  N13: M4.pin_2, M5.pin_2, S1.M1-01
  N14: S1.12V, U1.P, U2.IN+
  N15: U1.S, BAT1.+

notes:
  Lado Esquerdo
  Encoder E2-Q2
  Lado Direito

custom parts:
  DOIT Esp32 DevKit v1 (30 pins long, 11 pins width): The DOIT Esp32 DevKit v1 is one of the development board created by DOIT to evaluate the ESP-WROOM-32 module. It is based on the ESP32 microcontroller that boasts Wifi, Bluetooth, Ethernet and Low Power support all in a single chip. (vanepp) made breadboard work, adjusted pin numbering and labels and reduced size of schematic and cleaned up pcb. This chip is 30pins long (2 x15) and 11 pins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
  Adafruit VL530X Time of Flight Distance Sensor: The VL53L0X is a Time of Flight distance sensor like no other you've used! The sensor contains a very tiny invisible laser source, and a matching sensor. The VL53L0X can detect the "time of flight", or how long the light has taken to bounce back to the sensor. Since it uses a very narrow light source, it is good for determining distance of only the surface directly in front of it. Unlike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
  H-Bridge with L298N: h-bridge
  LM2596 step down module: LM2596 DC-DC step down power supply module 3 A.
